// Logisim project JMC.circ as structural Verilog: 6 circuits, main circuit main
module main (
);

  wire addr_ij, addr_imm, addr_pc, addr_sp, alu_in, alu_out, and_1_out, and_2_out, clock, comparator_1_eq,
       control_1_reg_in, dc_in, f_out, i_in, ir1_out, ir2_out, j_in, last, load_ir0, load_ir1, load_ir2,
       load_pc_ij, load_x, load_y, mem_in, mem_out, need_ir1, need_ir2, not_1_out, not_2_out, not_3_out,
       pc_inc, r0_out, r1_out, reg_in, reg_out, sp_dec, sp_inc, stop_if_zero, zero;
  wire [2:0] controlled_buffer_1_out, controlled_buffer_3_out, decoder_1_alu_op, decoder_1_reg0,
       decoder_1_reg1;
  wire [7:0] alu_1_d_out, alu_1_f_out, controlled_buffer_11_out, controlled_buffer_12_out,
       controlled_buffer_13_out, controlled_buffer_16_out, controlled_buffer_17_out, ir0, memory_1_data_out,
       registers_1_f_out, registers_1_r_out;
  wire [15:0] controlled_buffer_6_out, decoder_1_ir1, memory_1_pcl_out, memory_1_spl_out, registers_1_j_out;

  assign controlled_buffer_1_out = r1_out ? decoder_1_reg1 : 3'bz;  // Controlled_Buffer controlled_buffer_1
  assign controlled_buffer_1_out = r0_out ? decoder_1_reg0 : 3'bz;  // Controlled_Buffer controlled_buffer_2
  assign controlled_buffer_3_out = f_out ? 3'b111 : 3'bz;  // Controlled_Buffer controlled_buffer_3
  assign controlled_buffer_3_out = and_1_out ? decoder_1_reg0 : 3'bz;  // Controlled_Buffer controlled_buffer_4
  assign controlled_buffer_3_out = i_in ? 3'b100 : 3'bz;  // Controlled_Buffer controlled_buffer_5
  and and_1 (and_1_out, not_1_out, and_2_out);
  not not_1 (not_1_out, f_out);
  and and_2 (and_2_out, not_2_out, not_3_out);
  not not_2 (not_2_out, j_in);
  not not_3 (not_3_out, i_in);
  assign controlled_buffer_6_out = addr_ij ? registers_1_j_out : 16'bz;  // Controlled_Buffer controlled_buffer_6
  assign controlled_buffer_6_out = addr_imm ? decoder_1_ir1 : 16'bz;  // Controlled_Buffer controlled_buffer_7
  assign controlled_buffer_3_out = j_in ? 3'b101 : 3'bz;  // Controlled_Buffer controlled_buffer_8
  assign controlled_buffer_6_out = addr_sp ? memory_1_spl_out : 16'bz;  // Controlled_Buffer controlled_buffer_9
  assign controlled_buffer_6_out = addr_pc ? memory_1_pcl_out : 16'bz;  // Controlled_Buffer controlled_buffer_10
  Clock clock_1 (.out(clock));
  Memory memory_1 (
    .address(controlled_buffer_6_out), .data(controlled_buffer_11_out), .data_out(memory_1_data_out),
    .clock(clock), .ram_write(mem_in), .ram_read(mem_out), .sph_out(memory_1_spl_out[15:8]),
    .spl_out(memory_1_spl_out[7:0]), .sph_write(1'b0), .spl_write(1'b0), .pch_write(1'b0), .pcl_write(1'b0),
    .sp_inc(sp_inc), .sp_dec(sp_dec), .pc_inc(pc_inc), .i_in(registers_1_j_out[15:8]),
    .j_in(registers_1_j_out[7:0]), .load_pc_ij(load_pc_ij), .pch_out(memory_1_pcl_out[15:8]),
    .pcl_out(memory_1_pcl_out[7:0]));
  Registers registers_1 (
    .r_in(controlled_buffer_13_out), .r_out(registers_1_r_out), .i_out(registers_1_j_out[15:8]),
    .j_out(registers_1_j_out[7:0]), .f_out(registers_1_f_out), .in_selector(controlled_buffer_3_out),
    .clock(clock), .out_selector(controlled_buffer_1_out));
  assign controlled_buffer_11_out = mem_in ? controlled_buffer_12_out : 8'bz;  // Controlled_Buffer controlled_buffer_11
  assign controlled_buffer_12_out = mem_out ? memory_1_data_out : 8'bz;  // Controlled_Buffer controlled_buffer_12
  assign controlled_buffer_13_out = reg_in ? controlled_buffer_12_out : 8'bz;  // Controlled_Buffer controlled_buffer_13
  assign controlled_buffer_12_out = reg_out ? registers_1_r_out : 8'bz;  // Controlled_Buffer controlled_buffer_14
  assign controlled_buffer_12_out = ir1_out ? decoder_1_ir1[7:0] : 8'bz;  // Controlled_Buffer controlled_buffer_15
  Comparator comparator_1 (.a({8{1'b0}}), .b(controlled_buffer_12_out), .eq(comparator_1_eq));  // open: gt, lt
  assign controlled_buffer_16_out = dc_in ? controlled_buffer_12_out : 8'bz;  // Controlled_Buffer controlled_buffer_16
  assign controlled_buffer_17_out = alu_in ? controlled_buffer_12_out : 8'bz;  // Controlled_Buffer controlled_buffer_17
  assign controlled_buffer_12_out = f_out ? alu_1_f_out : 8'bz;  // Controlled_Buffer controlled_buffer_18
  assign controlled_buffer_12_out = alu_out ? alu_1_d_out : 8'bz;  // Controlled_Buffer controlled_buffer_19
  assign controlled_buffer_12_out = ir2_out ? decoder_1_ir1[15:8] : 8'bz;  // Controlled_Buffer controlled_buffer_20
  and and_3 (zero, comparator_1_eq, stop_if_zero);
  Decoder decoder_1 (
    .main_bus_in(controlled_buffer_16_out), .load_ir0(load_ir0), .load_ir1(load_ir1), .load_ir2(load_ir2),
    .clock(clock), .last(last), .ir0(ir0), .ir1(decoder_1_ir1[7:0]), .ir2(decoder_1_ir1[15:8]),
    .reg0(decoder_1_reg0), .reg1(decoder_1_reg1), .load_1(need_ir1), .load_2(need_ir2),
    .alu_op(decoder_1_alu_op));
  ALU alu_1 (
    .d_in(controlled_buffer_17_out), .d_out(alu_1_d_out), .f_out(alu_1_f_out), .f_in(registers_1_f_out),
    .clock(clock), .ldx(load_x), .ldy(load_y), .op(decoder_1_alu_op));
  Control control_1 (
    .ir0(ir0), .need_ir1(need_ir1), .need_ir2(need_ir2), .clock(clock), .zero(zero), .pc_inc(pc_inc),
    .dc_in(dc_in), .addr_pc(addr_pc), .j_in(j_in), .i_in(i_in), .mem_out(mem_out), .mem_in(mem_in),
    .addr_sp(addr_sp), .addr_ij(addr_ij), .addr_imm(addr_imm), .ir2_out(ir2_out), .ir1_out(ir1_out),
    .reg_in(control_1_reg_in), .r1_out(r1_out), .r0_out(r0_out), .load_f(f_out), .alu_out(alu_out),
    .load_x(load_x), .load_y(load_y), .sp_inc(sp_inc), .sp_dec(sp_dec), .load_pc_ij(load_pc_ij),
    .stop_if_zero(stop_if_zero), .load_ir0(load_ir0), .load_ir1(load_ir1), .load_ir2(load_ir2), .last(last));
  or or_1 (reg_in, f_out, control_1_reg_in);
  or or_2 (reg_out, r0_out, r1_out);
  or or_3 (alu_in, load_x, load_y);

  // Other names for the same wires on the sheet: load_f = f_out
endmodule

module ALU (
  input  [7:0] f_in,
  input  clock,
  input  ldx,
  input  ldy,
  input  [2:0] op,
  input  [7:0] d_in,
  output [7:0] d_out,
  output [7:0] f_out
);

  wire add_or_sub, and_1_out, and_2_out, and_3_out, and_4_out, b_out, c_out, demultiplexer_1_out0,
       demultiplexer_1_out1, demultiplexer_1_out2, demultiplexer_1_out3, demultiplexer_1_out4,
       demultiplexer_1_out5, demultiplexer_1_out6, not_1_out, not_2_out, not_3_out, not_4_out, o_out,
       overflow;
  wire [2:0] comparator_1_gt;
  wire [7:0] adder_1_out, adder_2_out, and_5_out, nor_1_out, or_2_out, subtractor_1_out, subtractor_2_out, x,
       y;

  not not_1 (not_1_out, x[7]);
  not not_2 (not_2_out, y[7]);
  not not_3 (not_3_out, clock);
  and and_1 (and_1_out, x[7], y[7]);
  not not_4 (not_4_out, d_out[7]);
  and and_2 (and_2_out, not_1_out, not_2_out);
  and and_3 (and_3_out, and_1_out, not_4_out);
  and and_4 (and_4_out, d_out[7], and_2_out);
  Multiplexer #(.enable("false")) multiplexer_1 (.in0(f_in[2]), .in1(overflow), .out(o_out), .sel(add_or_sub));
  Register u_X (.D(d_in), .en(ldx), .Q(x), .clk(not_3_out), .clr(1'b0));
  Register u_Y (.D(d_in), .en(ldy), .Q(y), .clk(not_3_out), .clr(1'b0));
  or or_1 (overflow, and_3_out, and_4_out);
  Adder adder_1 (.a(x), .b(y), .out(adder_1_out), .cin(1'b0), .cout(c_out));
  Adder adder_2 (.a(x), .b(y), .out(adder_2_out), .cin(f_in[0]), .cout(c_out));
  Subtractor subtractor_1 (.a(x), .b(y), .out(subtractor_1_out), .bin(1'b0), .bout(b_out));
  Subtractor subtractor_2 (.a(x), .b(y), .out(subtractor_2_out), .bin(f_in[1]), .bout(b_out));
  Comparator comparator_1 (.a(x), .b(y), .gt(comparator_1_gt[0]), .eq(comparator_1_gt[1]), .lt(comparator_1_gt[2]));
  assign d_out = demultiplexer_1_out0 ? adder_1_out : 8'bz;  // Controlled_Buffer controlled_buffer_1
  assign d_out = demultiplexer_1_out1 ? adder_2_out : 8'bz;  // Controlled_Buffer controlled_buffer_2
  assign d_out = demultiplexer_1_out2 ? subtractor_1_out : 8'bz;  // Controlled_Buffer controlled_buffer_3
  assign and_5_out = x & y;  // AND_Gate and_5, 8 bits wide
  assign or_2_out = x | y;  // OR_Gate or_2, 8 bits wide
  assign nor_1_out = ~(x | y);  // NOR_Gate nor_1, 8 bits wide
  Demultiplexer #(.select(3), .enable("false")) demultiplexer_1 (
    .out0(demultiplexer_1_out0), .out1(demultiplexer_1_out1), .out2(demultiplexer_1_out2),
    .out3(demultiplexer_1_out3), .out4(demultiplexer_1_out4), .out5(demultiplexer_1_out5),
    .out6(demultiplexer_1_out6), .in(1'b1), .sel(op));  // open: out7
  assign d_out = demultiplexer_1_out3 ? subtractor_2_out : 8'bz;  // Controlled_Buffer controlled_buffer_4
  assign d_out = demultiplexer_1_out4 ? and_5_out : 8'bz;  // Controlled_Buffer controlled_buffer_5
  assign d_out = demultiplexer_1_out5 ? or_2_out : 8'bz;  // Controlled_Buffer controlled_buffer_6
  assign d_out = demultiplexer_1_out6 ? nor_1_out : 8'bz;  // Controlled_Buffer controlled_buffer_7
  Multiplexer #(.width(8), .enable("false")) multiplexer_2 (
    .in0({2'b00, f_in[2:0], comparator_1_gt}), .in1({2'b00, o_out, b_out, c_out, f_in[2:0]}), .out(f_out),
    .sel(add_or_sub));
  or or_3 (add_or_sub, demultiplexer_1_out0, demultiplexer_1_out1, demultiplexer_1_out2, demultiplexer_1_out3);

  // Other names for the same wires on the sheet: c_in = f_in[0]; b_in = f_in[1]; o_in = f_in[2]; msb_o = d_out[7]
endmodule

module Registers (
  input  [2:0] in_selector,
  input  clock,
  input  [2:0] out_selector,
  input  [7:0] r_in,
  output [7:0] r_out,
  output [7:0] i_out,
  output [7:0] j_out,
  output [7:0] f_out
);

  wire demultiplexer_1_out0, demultiplexer_1_out1, demultiplexer_1_out2, demultiplexer_1_out3,
       demultiplexer_1_out4, demultiplexer_1_out5, demultiplexer_1_out6, demultiplexer_1_out7,
       demultiplexer_2_out0, demultiplexer_2_out1, demultiplexer_2_out2, demultiplexer_2_out3,
       demultiplexer_2_out4, demultiplexer_2_out5, demultiplexer_2_out6, demultiplexer_2_out7, not_1_out;
  wire [7:0] A_q, B_q, C_q, D_q, Z_q;

  Demultiplexer #(.select(3), .enable("false")) demultiplexer_1 (
    .out0(demultiplexer_1_out0), .out1(demultiplexer_1_out1), .out2(demultiplexer_1_out2),
    .out3(demultiplexer_1_out3), .out4(demultiplexer_1_out4), .out5(demultiplexer_1_out5),
    .out6(demultiplexer_1_out6), .out7(demultiplexer_1_out7), .in(1'b1), .sel(in_selector));
  not not_1 (not_1_out, clock);
  Register A (.D(r_in), .en(demultiplexer_1_out0), .Q(A_q), .clk(not_1_out), .clr(1'b0));
  Register B (.D(r_in), .en(demultiplexer_1_out1), .Q(B_q), .clk(not_1_out), .clr(1'b0));
  Register C (.D(r_in), .en(demultiplexer_1_out2), .Q(C_q), .clk(not_1_out), .clr(1'b0));
  Register D (.D(r_in), .en(demultiplexer_1_out3), .Q(D_q), .clk(not_1_out), .clr(1'b0));
  Register I (.D(r_in), .en(demultiplexer_1_out4), .Q(i_out), .clk(not_1_out), .clr(1'b0));
  Register J (.D(r_in), .en(demultiplexer_1_out5), .Q(j_out), .clk(not_1_out), .clr(1'b0));
  Register Z (.D(r_in), .en(demultiplexer_1_out6), .Q(Z_q), .clk(not_1_out), .clr(1'b0));
  Register F (.D(r_in), .en(demultiplexer_1_out7), .Q(f_out), .clk(not_1_out), .clr(1'b0));
  Demultiplexer #(.select(3), .enable("false")) demultiplexer_2 (
    .out0(demultiplexer_2_out0), .out1(demultiplexer_2_out1), .out2(demultiplexer_2_out2),
    .out3(demultiplexer_2_out3), .out4(demultiplexer_2_out4), .out5(demultiplexer_2_out5),
    .out6(demultiplexer_2_out6), .out7(demultiplexer_2_out7), .in(1'b1), .sel(out_selector));
  assign r_out = demultiplexer_2_out0 ? A_q : 8'bz;  // Controlled_Buffer controlled_buffer_1
  assign r_out = demultiplexer_2_out1 ? B_q : 8'bz;  // Controlled_Buffer controlled_buffer_2
  assign r_out = demultiplexer_2_out2 ? C_q : 8'bz;  // Controlled_Buffer controlled_buffer_3
  Controlled_Buffer #(.width(8)) controlled_buffer_4 (.in(D_q), .en(demultiplexer_2_out3));  // open: out
  assign r_out = demultiplexer_2_out4 ? i_out : 8'bz;  // Controlled_Buffer controlled_buffer_5
  assign r_out = demultiplexer_2_out5 ? j_out : 8'bz;  // Controlled_Buffer controlled_buffer_6
  assign r_out = demultiplexer_2_out6 ? Z_q : 8'bz;  // Controlled_Buffer controlled_buffer_7
  assign r_out = demultiplexer_2_out7 ? f_out : 8'bz;  // Controlled_Buffer controlled_buffer_8
endmodule

module Control (
  input  clock,
  input  zero,
  input  [7:0] ir0,
  input  need_ir1,
  input  need_ir2,
  output pc_inc,
  output dc_in,
  output addr_pc,
  output j_in,
  output i_in,
  output mem_out,
  output mem_in,
  output addr_sp,
  output addr_ij,
  output addr_imm,
  output ir2_out,
  output ir1_out,
  output reg_in,
  output r1_out,
  output r0_out,
  output load_f,
  output alu_out,
  output load_x,
  output load_y,
  output sp_inc,
  output sp_dec,
  output load_pc_ij,
  output stop_if_zero,
  output load_ir0,
  output load_ir1,
  output load_ir2,
  output last
);

  wire and_1_out, and_3_out, and_4_out, and_5_out, and_6_out, and_7_out, and_8_out, and_14_out,
       comparator_1_eq, comparator_1_gt, comparator_2_eq, comparator_2_gt, doing_mc, ir_loaded, not_1_out,
       not_2_out, not_4_out, not_5_out, not_6_out, not_7_out, not_8_out, not_9_out, or_1_out, or_2_out,
       or_4_out;
  wire [4:4] not_3_out;
  wire [7:0] counter_1_q, counter_2_q, counter_3_q;
  wire [15:0] rom_1_data;
  wire [15:5] controlled_buffer_1_out;

  and and_1 (and_1_out, clock, ir_loaded);
  not not_1 (not_1_out, and_3_out);
  and and_2 (doing_mc, and_1_out, not_1_out);
  and and_3 (and_3_out, and_1_out, counter_2_q[1]);
  Counter counter_1 (.Q(counter_1_q), .clk(and_4_out), .clr(and_6_out));  // open: load, D, count, carry
  and and_4 (and_4_out, clock, not_2_out);
  not not_2 (not_2_out, ir_loaded);
  Counter counter_2 (.count(doing_mc), .Q(counter_2_q), .clk(doing_mc), .clr(and_6_out));  // open: load, D, carry
  Counter counter_3 (.count(and_3_out), .Q(counter_3_q), .clk(and_3_out), .clr(and_6_out));  // open: load, D, carry
  not not_3 (not_3_out[4], ir0[3]);
  not not_4 (not_4_out, need_ir1);
  not not_5 (not_5_out, need_ir2);
  Comparator #(.width(2), .mode("unsigned")) comparator_1 (
    .a(counter_1_q[1:0]), .b(2'b01), .gt(comparator_1_gt), .eq(comparator_1_eq));  // open: lt
  Comparator #(.width(2), .mode("unsigned")) comparator_2 (
    .a(counter_1_q[1:0]), .b(2'b10), .gt(comparator_2_gt), .eq(comparator_2_eq));  // open: lt
  and and_5 (and_5_out, comparator_1_gt, and_7_out);
  or or_1 (or_1_out, zero, last);
  not not_6 (not_6_out, clock);
  and and_6 (and_6_out, or_1_out, not_6_out);
  and and_7 (and_7_out, not_5_out, not_4_out);
  and and_8 (and_8_out, comparator_2_gt, not_5_out);
  or or_2 (or_2_out, and_8_out, and_5_out);
  or or_3 (ir_loaded, counter_1_q[2], or_2_out);
  ROM #(.addrWidth(16), .dataWidth(16)) rom_1 (
    .addr({4'b0000, ir0[7:4], 3'b000, not_3_out[4], counter_3_q[3:0]}), .data(rom_1_data), .sel(1'b1));
  assign {controlled_buffer_1_out[15], last, controlled_buffer_1_out[13:5], ir2_out, ir1_out, reg_in, r1_out, r0_out} = ir_loaded ? rom_1_data : 16'bz;  // Controlled_Buffer controlled_buffer_1
  assign {controlled_buffer_1_out[15], last, controlled_buffer_1_out[13:5], ir2_out, ir1_out, reg_in, r1_out, r0_out} = not_7_out ? {16{1'b0}} : 16'bz;  // Controlled_Buffer controlled_buffer_2
  not not_7 (not_7_out, ir_loaded);
  not not_8 (not_8_out, ir_loaded);
  and and_9 (load_ir0, not_8_out, comparator_1_eq);
  and and_10 (load_ir1, not_8_out, comparator_2_eq);
  and and_11 (load_ir2, not_8_out, comparator_2_gt);
  not not_9 (not_9_out, controlled_buffer_1_out[15]);
  or or_4 (or_4_out, load_ir1, load_ir2);
  not not_10 (addr_pc, ir_loaded);
  and and_12 (j_in, controlled_buffer_1_out[11], controlled_buffer_1_out[15]);
  and and_13 (i_in, controlled_buffer_1_out[10], controlled_buffer_1_out[15]);
  and and_14 (and_14_out, controlled_buffer_1_out[9], controlled_buffer_1_out[15]);
  and and_15 (mem_in, controlled_buffer_1_out[8], controlled_buffer_1_out[15]);
  and and_16 (addr_sp, controlled_buffer_1_out[7], controlled_buffer_1_out[15]);
  and and_17 (addr_ij, controlled_buffer_1_out[6], controlled_buffer_1_out[15]);
  and and_18 (addr_imm, controlled_buffer_1_out[5], controlled_buffer_1_out[15]);
  and and_19 (load_f, controlled_buffer_1_out[5], not_9_out);
  and and_20 (alu_out, controlled_buffer_1_out[6], not_9_out);
  and and_21 (load_x, controlled_buffer_1_out[7], not_9_out);
  and and_22 (load_y, controlled_buffer_1_out[8], not_9_out);
  and and_23 (sp_inc, controlled_buffer_1_out[9], not_9_out);
  and and_24 (sp_dec, controlled_buffer_1_out[10], not_9_out);
  and and_25 (load_pc_ij, controlled_buffer_1_out[11], not_9_out);
  and and_26 (stop_if_zero, controlled_buffer_1_out[12], not_9_out);
  or or_5 (pc_inc, doing_mc, or_4_out);
  or or_6 (mem_out, addr_pc, and_14_out);

  assign dc_in = addr_pc;

  // Notes on the sheet:
  //   contents of rom_1 (hex, n*v repeats v):
  //   200 c181 14*0 200 c188 238*0 8284 4400 254*0 1001 4800 14*0 1008 4800 238*0 4006 15*0 400c 239*0
  //   c244 15*0 c224 239*0 c141 15*0 c121 255*0 880c c414 494*0 81 102 44 4020 12*0 81 108 44 4020 236*0
  //   81 102 44 4020 12*0 81 108 44 4020 236*0 81 102 44 4020 12*0 81 108 44 4020 236*0 81 102 44 4020
  //   12*0 81 108 44 4020 236*0 81 102 44 4020 12*0 81 108 44 4020 236*0 81 102 44 4020 12*0 81 108 44
  //   4020 236*0 81 102 44 4020 12*0 81 108 44 4020 236*0 81 102 44 4020 12*0 81 108 44 4020
endmodule

module Decoder (
  input  load_ir0,
  input  load_ir1,
  input  load_ir2,
  input  clock,
  input  last,
  input  [7:0] main_bus_in,
  output [7:0] ir0,
  output [7:0] ir1,
  output [7:0] ir2,
  output [2:0] reg0,
  output [2:0] reg1,
  output load_1,
  output load_2,
  output [2:0] alu_op
);

  wire adc, add, \and , and_1_out, and_2_out, and_3_out, cmp, const_args, jnz, lda, lw, mw, \nor , not_2_out,
       \or , or_1_out, or_2_out, or_3_out, or_4_out, pop, push, sbb, sub, sw, unused_instruction;

  Demultiplexer #(.select(4), .enable("false")) demultiplexer_1 (
    .out0(push), .out1(pop), .out2(jnz), .out3(mw), .out4(lw), .out5(sw), .out6(lda),
    .out7(unused_instruction), .out8(add), .out9(adc), .out10(sub), .out11(sbb), .out12(\and ), .out13(\or ),
    .out14(\nor ), .out15(cmp), .in(1'b1), .sel({ir0[7], alu_op}));
  not not_1 (const_args, ir0[3]);
  or or_1 (or_1_out, push, jnz);
  or or_2 (or_2_out, ir0[7], mw);
  and and_1 (and_1_out, const_args, or_1_out);
  or or_3 (or_3_out, lw, sw);
  not not_2 (not_2_out, clock);
  and and_2 (and_2_out, not_2_out, last);
  Register u_IR0 (.D(main_bus_in), .en(load_ir0), .Q({ir0[7], alu_op, ir0[3:0]}), .clk(clock), .clr(and_2_out));
  Register u_IR1 (.D(main_bus_in), .en(load_ir1), .Q(ir1), .clk(clock), .clr(and_2_out));
  Register u_IR2 (.D(main_bus_in), .en(load_ir2), .Q(ir2), .clk(clock), .clr(and_2_out));
  or or_4 (or_4_out, or_2_out, and_1_out);
  and and_3 (and_3_out, const_args, or_3_out);
  or or_5 (load_1, or_4_out, load_2);
  or or_6 (load_2, lda, and_3_out);

  assign ir0[6:4] = alu_op;
  assign reg0 = ir0[2:0];
  assign reg1 = ir1[2:0];

  // Other names for the same wires on the sheet: alu_op_t = ir0[7]; reg_args = ir0[3]
endmodule

module Memory (
  input  clock,
  input  ram_write,
  input  ram_read,
  input  sph_write,
  input  spl_write,
  input  pch_write,
  input  pcl_write,
  input  sp_inc,
  input  sp_dec,
  input  pc_inc,
  input  [15:0] address,
  input  [7:0] data,
  input  [7:0] i_in,
  input  [7:0] j_in,
  input  load_pc_ij,
  output [7:0] data_out,
  output [7:0] sph_out,
  output [7:0] spl_out,
  output [7:0] pch_out,
  output [7:0] pcl_out
);

  wire and_1_out, and_2_out, and_3_out, and_4_out, and_5_out, and_6_out, and_7_out, and_8_out, and_9_out,
       counter_2_carry, counter_4_carry, demultiplexer_1_out12, demultiplexer_1_out13, demultiplexer_1_out14,
       demultiplexer_1_out15, not_1_out, not_2_out, not_3_out, not_4_out, not_5_out, not_6_out, or_1_out,
       or_2_out, or_3_out, or_4_out, or_5_out, or_6_out, or_7_out, or_8_out, or_9_out, or_10_out, or_11_out,
       or_12_out;
  wire [7:0] controlled_buffer_2_out, controlled_buffer_3_out, ram_1_data, rom_1_data;

  and and_1 (and_1_out, address[10], address[15], address[14], address[13], address[12], address[11], address[9], address[8], address[7], address[6], address[5], address[4]);
  Demultiplexer #(.select(4), .enable("false")) demultiplexer_1 (
    .out12(demultiplexer_1_out12), .out13(demultiplexer_1_out13), .out14(demultiplexer_1_out14),
    .out15(demultiplexer_1_out15), .in(and_1_out), .sel(address[3:0]));  // open: out0, out1, out2, out3, out4, out5, out6, out7, out8, out9, out10, out11
  and and_2 (and_2_out, not_2_out, not_1_out);
  assign address = and_2_out ? {16{1'b0}} : 16'bz;  // Controlled_Buffer controlled_buffer_1
  not not_1 (not_1_out, ram_read);
  not not_2 (not_2_out, ram_write);
  assign controlled_buffer_2_out = load_pc_ij ? i_in : 8'bz;  // Controlled_Buffer controlled_buffer_2
  not not_3 (not_3_out, clock);
  not not_4 (not_4_out, clock);
  or or_1 (or_1_out, sph_write, demultiplexer_1_out15);
  or or_2 (or_2_out, spl_write, demultiplexer_1_out14);
  or or_3 (or_3_out, pch_write, demultiplexer_1_out13);
  or or_4 (or_4_out, pcl_write, demultiplexer_1_out12);
  assign controlled_buffer_3_out = load_pc_ij ? j_in : 8'bz;  // Controlled_Buffer controlled_buffer_3
  or or_5 (or_5_out, ram_read, ram_write);
  not not_5 (not_5_out, address[15]);
  ROM #(.addrWidth(15)) rom_1 (.addr(address[14:0]), .data(rom_1_data), .sel(1'b1));
  RAM #(.addrWidth(15)) ram_1 (
    .addr(address[14:0]), .data(ram_1_data), .sel(or_5_out), .clk(not_3_out), .ld(ram_read), .clr(1'b0));
  assign ram_1_data = and_3_out ? data : 8'bz;  // Controlled_Buffer controlled_buffer_4
  and and_3 (and_3_out, ram_write, address[15]);
  or or_6 (or_6_out, load_pc_ij, or_3_out);
  or or_7 (or_7_out, load_pc_ij, or_4_out);
  not not_6 (not_6_out, load_pc_ij);
  assign data_out = not_5_out ? rom_1_data : 8'bz;  // Controlled_Buffer controlled_buffer_5
  assign data_out = and_4_out ? ram_1_data : 8'bz;  // Controlled_Buffer controlled_buffer_6
  and and_4 (and_4_out, address[15], ram_read);
  assign controlled_buffer_2_out = not_6_out ? data : 8'bz;  // Controlled_Buffer controlled_buffer_7
  assign controlled_buffer_3_out = not_6_out ? data : 8'bz;  // Controlled_Buffer controlled_buffer_8
  or or_8 (or_8_out, sp_dec, or_1_out);
  or or_9 (or_9_out, sp_dec, or_2_out);
  Counter counter_1 (
    .load(or_8_out), .D(controlled_buffer_2_out), .count(or_12_out), .Q(sph_out), .clk(or_10_out));  // open: carry, clr
  or or_10 (or_10_out, and_7_out, and_9_out);
  Counter counter_2 (
    .load(or_9_out), .D(controlled_buffer_3_out), .count(or_12_out), .Q(spl_out), .carry(counter_2_carry),
    .clk(and_8_out));  // open: clr
  Counter counter_3 (
    .load(or_6_out), .D(controlled_buffer_2_out), .Q(pch_out), .clk(and_5_out));  // open: count, carry, clr
  and and_5 (and_5_out, and_6_out, counter_4_carry);
  Counter counter_4 (
    .load(or_7_out), .D(controlled_buffer_3_out), .count(and_6_out), .Q(pcl_out), .carry(counter_4_carry),
    .clk(and_6_out));  // open: clr
  and and_6 (and_6_out, not_4_out, pc_inc);
  and and_7 (and_7_out, and_8_out, counter_2_carry);
  or or_11 (or_11_out, or_2_out, or_12_out);
  and and_8 (and_8_out, or_11_out, not_4_out);
  and and_9 (and_9_out, or_1_out, not_4_out);
  or or_12 (or_12_out, sp_inc, sp_dec);

  // Notes on the sheet:
  //   contents of rom_1 (hex, n*v repeats v):
  //   60 2 80 60 2 80 30 1 55 fe ff 54 ff ff 0 1 0 1
endmodule
